// Logisim project control_logic.circ as structural Verilog: 1 circuit, main circuit control_logic
module control_logic (
  input  [31:0] inst,
  input  BrEq,
  input  BrLt,
  output PCSel,
  output RegWEn,
  output [2:0] ImmSel,
  output BrUn,
  output ASel,
  output BSel,
  output [3:0] ALUSel,
  output MemRW,
  output [1:0] WBSel,
  output CSRSel,
  output CSRWen
);

  wire comparator_1_eq, comparator_2_eq, comparator_3_eq, comparator_4_eq, comparator_5_eq, comparator_6_eq,
       comparator_9_eq, comparator_10_eq, comparator_12_eq, comparator_13_eq, comparator_14_eq,
       comparator_15_eq, comparator_16_eq, comparator_17_eq, comparator_18_eq, comparator_19_eq,
       comparator_20_eq, comparator_21_eq, comparator_22_eq, comparator_23_eq, comparator_24_eq,
       comparator_25_eq, comparator_26_eq, comparator_27_eq, comparator_28_eq, comparator_29_eq, ImmB,
       ImmCSR, ImmS, ImmU, ImmUJ, isIorR, isMul, isMulh, isSra, isSub, or_3_out;
  wire [2:0] multiplexer_2_out, multiplexer_3_out, multiplexer_5_out, multiplexer_8_out;
  wire [3:0] multiplexer_1_out, multiplexer_4_out, multiplexer_6_out, multiplexer_7_out, multiplexer_10_out;

  Multiplexer #(.enable("false"), .select(3), .width(4)) multiplexer_1 (
    .in0(4'b0000), .in1(4'b0110), .in2(4'b0111), .in3(4'b1011), .in4(4'b0011), .in5(4'b0100), .in6(4'b0010),
    .in7(4'b0001), .out(multiplexer_1_out), .sel(inst[14:12]));
  Multiplexer #(.enable("false"), .width(3)) multiplexer_2 (
    .in0(3'b000), .in1(3'b001), .out(multiplexer_2_out), .sel(ImmS));
  Comparator #(.width(7)) comparator_1 (.a(inst[31:25]), .b(7'b0000001), .eq(comparator_1_eq));  // open: gt, lt
  Comparator #(.width(3)) comparator_2 (.a(inst[14:12]), .b(3'b000), .eq(comparator_2_eq));  // open: gt, lt
  Comparator #(.width(7)) comparator_3 (.a(inst[6:0]), .b(7'b0110011), .eq(comparator_3_eq));  // open: gt, lt
  Comparator #(.width(7)) comparator_4 (.a(inst[31:25]), .b(7'b0000001), .eq(comparator_4_eq));  // open: gt, lt
  Comparator #(.width(3)) comparator_5 (.a(inst[14:12]), .b(3'b001), .eq(comparator_5_eq));  // open: gt, lt
  Comparator #(.width(7)) comparator_6 (.a(inst[6:0]), .b(7'b0110011), .eq(comparator_6_eq));  // open: gt, lt
  Multiplexer #(.enable("false"), .width(3)) multiplexer_3 (
    .in0(multiplexer_2_out), .in1(3'b010), .out(multiplexer_3_out), .sel(ImmB));
  Multiplexer #(.enable("false"), .width(4)) multiplexer_4 (
    .in0(multiplexer_1_out), .in1(4'b1010), .out(multiplexer_4_out), .sel(isMul));
  and and_1 (isMul, comparator_1_eq, comparator_2_eq, comparator_3_eq);
  and and_2 (isMulh, comparator_4_eq, comparator_5_eq, comparator_6_eq);
  Comparator #(.width(7)) comparator_7 (.a(inst[6:0]), .b(7'b0100011), .eq(ImmS));  // open: gt, lt
  Comparator #(.width(7)) comparator_8 (.a(inst[6:0]), .b(7'b1100011), .eq(ImmB));  // open: gt, lt
  Comparator #(.width(7)) comparator_9 (.a(inst[6:0]), .b(7'b0010111), .eq(comparator_9_eq));  // open: gt, lt
  Comparator #(.width(7)) comparator_10 (.a(inst[6:0]), .b(7'b0110111), .eq(comparator_10_eq));  // open: gt, lt
  Comparator #(.width(7)) comparator_11 (.a(inst[6:0]), .b(7'b1101111), .eq(ImmUJ));  // open: gt, lt
  Comparator #(.width(7)) comparator_12 (.a(inst[6:0]), .b(7'b1110011), .eq(comparator_12_eq));  // open: gt, lt
  Comparator #(.width(3)) comparator_13 (.a(inst[14:12]), .b(3'b101), .eq(comparator_13_eq));  // open: gt, lt
  Multiplexer #(.enable("false"), .width(3)) multiplexer_5 (
    .in0(multiplexer_3_out), .in1(3'b011), .out(multiplexer_5_out), .sel(ImmU));
  Comparator #(.width(7)) comparator_14 (.a(inst[6:0]), .b(7'b1110011), .eq(comparator_14_eq));  // open: gt, lt
  Comparator #(.width(3)) comparator_15 (.a(inst[14:12]), .b(3'b101), .eq(comparator_15_eq));  // open: gt, lt
  Multiplexer #(.enable("false"), .width(4)) multiplexer_6 (
    .in0(multiplexer_4_out), .in1(4'b1011), .out(multiplexer_6_out), .sel(isMulh));
  or or_1 (ImmU, comparator_9_eq, comparator_10_eq);
  or or_2 (ImmCSR, comparator_12_eq, comparator_13_eq);
  or or_3 (or_3_out, comparator_14_eq, comparator_15_eq);
  Multiplexer #(.enable("false"), .width(4)) multiplexer_7 (
    .in0(multiplexer_6_out), .in1(4'b1100), .out(multiplexer_7_out), .sel(isSub));
  Multiplexer #(.enable("false"), .width(3)) multiplexer_8 (
    .in0(multiplexer_5_out), .in1(3'b100), .out(multiplexer_8_out), .sel(ImmUJ));
  Multiplexer #(.enable("false"), .width(3)) multiplexer_9 (
    .in0(multiplexer_8_out), .in1(3'b101), .out(ImmSel), .sel(ImmCSR));
  and and_3 (BrUn, ImmB, or_3_out);
  Multiplexer #(.enable("false"), .width(4)) multiplexer_10 (
    .in0(multiplexer_7_out), .in1(4'b1100), .out(multiplexer_10_out), .sel(isSra));
  Comparator #(.width(7)) comparator_16 (.a(inst[31:25]), .b(7'b0100000), .eq(comparator_16_eq));  // open: gt, lt
  Comparator #(.width(3)) comparator_17 (.a(inst[14:12]), .b(3'b000), .eq(comparator_17_eq));  // open: gt, lt
  Comparator #(.width(7)) comparator_18 (.a(inst[6:0]), .b(7'b0110011), .eq(comparator_18_eq));  // open: gt, lt
  Comparator #(.width(7)) comparator_19 (.a(inst[31:25]), .b(7'b0100000), .eq(comparator_19_eq));  // open: gt, lt
  Comparator #(.width(3)) comparator_20 (.a(inst[14:12]), .b(3'b101), .eq(comparator_20_eq));  // open: gt, lt
  Multiplexer #(.enable("false"), .width(4)) multiplexer_11 (
    .in0(4'b0000), .in1(multiplexer_10_out), .out(ALUSel), .sel(isIorR));
  and and_4 (isSub, comparator_16_eq, comparator_17_eq, comparator_18_eq);
  and and_5 (isSra, comparator_19_eq, comparator_20_eq);
  Comparator #(.width(7)) comparator_21 (.a(inst[6:0]), .b(7'b0110011), .eq(comparator_21_eq));  // open: gt, lt
  Comparator #(.width(7)) comparator_22 (.a(inst[6:0]), .b(7'b0010011), .eq(comparator_22_eq));  // open: gt, lt
  Comparator #(.width(7)) comparator_23 (.a(inst[6:0]), .b(7'b0110011), .eq(comparator_23_eq));  // open: gt, lt
  Comparator #(.width(7)) comparator_24 (.a(inst[6:0]), .b(7'b0000011), .eq(comparator_24_eq));  // open: gt, lt
  Comparator #(.width(7)) comparator_25 (.a(inst[6:0]), .b(7'b0010011), .eq(comparator_25_eq));  // open: gt, lt
  Comparator #(.width(7)) comparator_26 (.a(inst[6:0]), .b(7'b1101111), .eq(comparator_26_eq));  // open: gt, lt
  Comparator #(.width(7)) comparator_27 (.a(inst[6:0]), .b(7'b0110111), .eq(comparator_27_eq));  // open: gt, lt
  Comparator #(.width(7)) comparator_28 (.a(inst[6:0]), .b(7'b0010111), .eq(comparator_28_eq));  // open: gt, lt
  Comparator #(.width(7)) comparator_29 (.a(inst[6:0]), .b(7'b1100111), .eq(comparator_29_eq));  // open: gt, lt
  or or_4 (isIorR, comparator_21_eq, comparator_22_eq);
  or or_5 (RegWEn, comparator_23_eq, comparator_24_eq, comparator_25_eq, comparator_26_eq, comparator_27_eq, comparator_28_eq, comparator_29_eq);

  // Other names for the same wires on the sheet: op[6:0] = inst[6:0]; rd[4:0] = inst[11:7]; funct3[2:0] = inst[14:12];
  //   rs1[4:0] = inst[19:15]; rs2[4:0] = inst[24:20]; funct7[6:0] = inst[31:25]

  // Notes on the sheet:
  //   INPUTS to your circuit
  //   decode
  //   Imm select: I, S, B, U, J, CSR
  //   ALU select
  //   DON'T CHANGE THE LOCATIONS OF THE INPUTS AND OUTPUTS!
  //   OUTPUT from your circuit
  //   Register Write Enable
endmodule
