// Logisim project imm_gen.circ as structural Verilog: 1 circuit, main circuit imm_gen
module imm_gen (
  input  [31:0] inst,
  input  [2:0] ImmSel,
  output [31:0] imm
);

  assign imm = {{20{inst[31]}}, inst[31:20]};  // Bit_Extender bit_extender_1

  // Other names for the same wires on the sheet: op[6:0] = inst[6:0]; rd[4:0] = inst[11:7]; funct3[2:0] = inst[14:12];
  //   rs1[4:0] = inst[19:15]; initial_imm[11:0] = inst[31:20]

  // Notes on the sheet:
  //   INPUTS to your circuit
  //   DON'T CHANGE THE LOCATIONS OF THE INPUTS AND OUTPUTS!
  //   OUTPUT from your circuit
endmodule
